// Digital circuit 4_bit_gpr.dig as structural Verilog
module _4_bit_gpr (
  input  [1:0] write__store__reset__load,
  input  [3:0] \input ,
  input  clk,
  output [3:0] \output 
);

  wire [3:0] multiplexer_1_out, not_1_out;

  Multiplexer #(.Selector_Bits(2), .Bits(4)) multiplexer_1 (
    .sel(write__store__reset__load), .in_0(\output ), .in_1(\input ), .in_2(4'b0000), .in_3(not_1_out),
    .out(multiplexer_1_out));
  assign not_1_out = ~4'b0000;  // Not not_1, 4 bits wide
  D_FF d_ff_1 (.D(multiplexer_1_out[3]), .C(clk), .Q(\output [3]));  // open: nQ
  D_FF d_ff_2 (.D(multiplexer_1_out[2]), .C(clk), .Q(\output [2]));  // open: nQ
  D_FF d_ff_3 (.D(multiplexer_1_out[1]), .C(clk), .Q(\output [1]));  // open: nQ
  D_FF d_ff_4 (.D(multiplexer_1_out[0]), .C(clk), .Q(\output [0]));  // open: nQ
endmodule
