// Digital circuit 4_bit_memory.dig as structural Verilog
module _4_bit_memory (
  input  [1:0] ctrl,
  input  [3:0] \input ,
  input  clk,
  input  [1:0] address,
  output [3:0] \output 
);

  wire and_1_out, and_2_out, and_3_out, and_4_out, decoder_1_out_0, decoder_1_out_1, decoder_1_out_2,
       decoder_1_out_3;
  wire [3:0] _4_bit_gpr_1_output, _4_bit_gpr_2_output, _4_bit_gpr_3_output, _4_bit_gpr_4_output;

  Decoder #(.Selector_Bits(2)) decoder_1 (
    .sel(address), .out_0(decoder_1_out_0), .out_1(decoder_1_out_1), .out_2(decoder_1_out_2),
    .out_3(decoder_1_out_3));
  and and_1 (and_1_out, clk, decoder_1_out_0);
  and and_2 (and_2_out, clk, decoder_1_out_1);
  and and_3 (and_3_out, clk, decoder_1_out_2);
  and and_4 (and_4_out, clk, decoder_1_out_3);
  _4_bit_gpr _4_bit_gpr_1 (
    .write__store__reset__load(ctrl), .\input (\input ), .clk(and_1_out), .\output (_4_bit_gpr_1_output));
  _4_bit_gpr _4_bit_gpr_2 (
    .write__store__reset__load(ctrl), .\input (\input ), .clk(and_2_out), .\output (_4_bit_gpr_2_output));
  _4_bit_gpr _4_bit_gpr_3 (
    .write__store__reset__load(ctrl), .\input (\input ), .clk(and_3_out), .\output (_4_bit_gpr_3_output));
  _4_bit_gpr _4_bit_gpr_4 (
    .write__store__reset__load(ctrl), .\input (\input ), .clk(and_4_out), .\output (_4_bit_gpr_4_output));
  Multiplexer #(.Selector_Bits(2), .Bits(4)) multiplexer_1 (
    .sel(address), .in_0(_4_bit_gpr_1_output), .in_1(_4_bit_gpr_2_output), .in_2(_4_bit_gpr_3_output),
    .in_3(_4_bit_gpr_4_output), .out(\output ));
endmodule
