// Digital circuit 4bit_instruction_register.dig as structural Verilog
module _4bit_instruction_register (
  input  [3:0] \input ,
  input  [1:0] ctrl,
  input  clk,
  output [3:0] \output 
);

  _4_bit_gpr _4_bit_gpr_1 (.write__store__reset__load(ctrl), .\input (\input ), .clk(clk), .\output (\output ));
endmodule
