// Digital circuit memory_register_dram.dig as structural Verilog
module memory_register_dram (
  input  pc_orind,
  input  [1:0] address,
  input  [3:0] input_mem,
  input  [1:0] ctrl_mem,
  input  [1:0] ctrl_ir__store__reset__load,
  input  [1:0] ctrl_pc__inc__reset__load,
  input  clk,
  output [3:0] out_8
);

  wire [1:0] _4bit_program_counter_1_p3, multiplexer_1_out;
  wire [3:0] _4_bit_memory_1_output;
  wire [3:2] _4bit_program_counter_1_p3_2;

  Multiplexer #(.Bits(2)) multiplexer_1 (
    .sel(pc_orind), .in_0(_4bit_program_counter_1_p3), .in_1(address), .out(multiplexer_1_out));
  _4_bit_memory _4_bit_memory_1 (
    .ctrl(ctrl_mem), .\input (input_mem), .clk(clk), .address(multiplexer_1_out),
    .\output (_4_bit_memory_1_output));
  // _4bit_program_counter _4bit_program_counter_1: pin names not known; wires that end beside it: clk, ctrl_pc__inc__reset__load, {_4bit_program_counter_1_p3_2, _4bit_program_counter_1_p3}
  _4bit_instruction_register _4bit_instruction_register_1 (
    .\input (_4_bit_memory_1_output), .ctrl(ctrl_ir__store__reset__load), .clk(clk), .\output (out_8));
endmodule
